// Logisim project Datapath_pipeline.circ as structural Verilog: 5 circuits, main circuit RF8
module RF8 (
  input  [2:0] rs1,
  input  [2:0] rs2,
  input  [2:0] rd3,
  input  RF8_en,
  input  RegW,
  input  clk,
  input  [31:0] wdata,
  output [31:0] rdata1,
  output [31:0] rdata2
);

  wire and_1_out, decoder_1_out0, decoder_1_out1, decoder_1_out3, decoder_1_out4, decoder_1_out5,
       decoder_1_out6, decoder_1_out7;
  wire [31:0] register_1_q, register_2_q, register_3_q, register_4_q, register_5_q, register_6_q,
       register_7_q, register_8_q;

  and and_1 (and_1_out, RF8_en, RegW);
  Decoder #(.select(3), .tristate("false"), .disabled(0), .enable("true")) decoder_1 (
    .out0(decoder_1_out0), .out1(decoder_1_out1), .out2(decoder_1_out1), .out3(decoder_1_out3),
    .out4(decoder_1_out4), .out5(decoder_1_out5), .out6(decoder_1_out6), .out7(decoder_1_out7), .sel(rd3),
    .en(and_1_out));
  Register #(.width(32), .trigger("rising"), .Select("low")) register_1 (
    .D(wdata), .en(decoder_1_out0), .Q(register_1_q), .clk(clk));  // open: clr
  Register #(.width(32), .trigger("rising"), .Select("low")) register_2 (
    .D(wdata), .en(decoder_1_out1), .Q(register_2_q), .clk(clk));  // open: clr
  Register #(.width(32), .trigger("rising"), .Select("low")) register_3 (
    .D(wdata), .en(decoder_1_out1), .Q(register_3_q), .clk(clk));  // open: clr
  Register #(.width(32), .trigger("rising"), .Select("low")) register_4 (
    .D(wdata), .en(decoder_1_out3), .Q(register_4_q), .clk(clk));  // open: clr
  Register #(.width(32), .trigger("rising"), .Select("low")) register_5 (
    .D(wdata), .en(decoder_1_out4), .Q(register_5_q), .clk(clk));  // open: clr
  Register #(.width(32), .trigger("rising"), .Select("low")) register_6 (
    .D(wdata), .en(decoder_1_out5), .Q(register_6_q), .clk(clk));  // open: clr
  Register #(.width(32), .trigger("rising"), .Select("low")) register_7 (
    .D(wdata), .en(decoder_1_out6), .Q(register_7_q), .clk(clk));  // open: clr
  Register #(.width(32), .trigger("rising"), .Select("low")) register_8 (
    .D(wdata), .en(decoder_1_out7), .Q(register_8_q), .clk(clk));  // open: clr
  Multiplexer #(.select(3), .width(32), .disabled("Z"), .enable("false")) multiplexer_1 (
    .in0(register_1_q), .in1(register_2_q), .in2(register_3_q), .in3(register_4_q), .in4(register_5_q),
    .in5(register_6_q), .in6(register_7_q), .in7(register_8_q), .out(rdata1), .sel(rs1));
  Multiplexer #(.select(3), .width(32), .disabled("Z"), .enable("false")) multiplexer_2 (
    .in0(register_1_q), .in1(register_2_q), .in2(register_3_q), .in3(register_4_q), .in4(register_5_q),
    .in5(register_6_q), .in6(register_7_q), .in7(register_8_q), .out(rdata2), .sel(rs2));
  // Probe on rdata1
  // Probe on rdata2

  // Other names for the same wires on the sheet: rd_en = RF8_en

  // Notes on the sheet:
  //   rdata1: pull=down
  //   wdata: pull=down
  //   rdata2: pull=down
  //   rd3: pull=down
  //   rs1: pull=down
  //   RF8_en: pull=down
  //   rs2: pull=down
  //   输入引脚区
  //   rs1, rs2, rd3分别只取相应寄存器号的低3位。当完整的目标寄存器号的高两位对应本组寄存器时，RF8_en=1（本组寄存器可写），否则RF8_en=0（本组寄存器禁写）
  //   输出引脚区
endmodule

// Register File
module RF32 (
  input  [4:0] rs1,
  input  [4:0] rs2,
  input  [4:0] rd,
  input  RegW,
  input  clk,
  input  [31:0] wdata,
  output [31:0] rdata1,
  output [31:0] rdata2
);

  wire decoder_1_out0, decoder_1_out1, decoder_1_out2, decoder_1_out3;
  wire [2:0] demultiplexer_1_out0, demultiplexer_1_out1, demultiplexer_1_out2, demultiplexer_1_out3,
       demultiplexer_2_out0, demultiplexer_2_out1, demultiplexer_2_out2, demultiplexer_2_out3;
  wire [31:0] rf8_1_rdata1, rf8_1_rdata2, rf8_2_rdata1, rf8_2_rdata2, rf8_3_rdata1, rf8_3_rdata2,
       rf8_4_rdata1, rf8_4_rdata2;

  Decoder #(.select(2), .tristate("false"), .disabled("Z"), .enable("false")) decoder_1 (
    .out0(decoder_1_out0), .out1(decoder_1_out1), .out2(decoder_1_out2), .out3(decoder_1_out3), .sel(rd[4:3]));
  Demultiplexer #(.select(2), .width(3), .tristate("false"), .disabled("Z"), .enable("false")) demultiplexer_1 (
    .out0(demultiplexer_1_out0), .out1(demultiplexer_1_out1), .out2(demultiplexer_1_out2),
    .out3(demultiplexer_1_out3), .in(rs1[2:0]), .sel(rs1[4:3]));
  Demultiplexer #(.select(2), .width(3), .tristate("false"), .disabled("Z"), .enable("false")) demultiplexer_2 (
    .out0(demultiplexer_2_out0), .out1(demultiplexer_2_out1), .out2(demultiplexer_2_out2),
    .out3(demultiplexer_2_out3), .in(rs2[2:0]), .sel(rs2[4:3]));
  RF8 rf8_1 (
    .rs1(demultiplexer_1_out0), .wdata(wdata), .RegW(RegW), .rdata1(rf8_1_rdata1), .rdata2(rf8_1_rdata2),
    .rs2(demultiplexer_2_out0), .RF8_en(decoder_1_out0), .rd3(rd[2:0]), .clk(clk));
  RF8 rf8_2 (
    .rs1(demultiplexer_1_out1), .wdata(wdata), .RegW(RegW), .rdata1(rf8_2_rdata1), .rdata2(rf8_2_rdata2),
    .rs2(demultiplexer_2_out1), .RF8_en(decoder_1_out1), .rd3(rd[2:0]), .clk(clk));
  RF8 rf8_3 (
    .rs1(demultiplexer_1_out2), .wdata(wdata), .RegW(RegW), .rdata1(rf8_3_rdata1), .rdata2(rf8_3_rdata2),
    .rs2(demultiplexer_2_out2), .RF8_en(decoder_1_out2), .rd3(rd[2:0]), .clk(clk));
  RF8 rf8_4 (
    .rs1(demultiplexer_1_out3), .wdata(wdata), .RegW(RegW), .rdata1(rf8_4_rdata1), .rdata2(rf8_4_rdata2),
    .rs2(demultiplexer_2_out3), .RF8_en(decoder_1_out3), .rd3(rd[2:0]), .clk(clk));
  Multiplexer #(.select(2), .width(32), .disabled("Z"), .enable("false")) multiplexer_1 (
    .in0(rf8_1_rdata1), .in1(rf8_2_rdata1), .in2(rf8_3_rdata1), .in3(rf8_4_rdata1), .out(rdata1),
    .sel(rs1[4:3]));
  Multiplexer #(.select(2), .width(32), .disabled("Z"), .enable("false")) multiplexer_2 (
    .in0(rf8_1_rdata2), .in1(rf8_2_rdata2), .in2(rf8_3_rdata2), .in3(rf8_4_rdata2), .out(rdata2),
    .sel(rs2[4:3]));

  // Notes on the sheet:
  //   rs1: pull=down
  //   wdata: pull=down
  //   rs2: pull=down
  //   rdata2: pull=down
  //   rdata1: pull=down
  //   rd: pull=down
  //   输入引脚区
  //   请勿改动引脚区
  //   输出引脚区
endmodule

module ALU (
  input  [3:0] ALUctr,
  input  [31:0] A,
  input  [31:0] B,
  output [31:0] Result
);

  wire comparator_1_lt, comparator_2_lt;
  wire [31:0] adder_1_out, and_1_out, bit_extender_1_out, bit_extender_2_out, demultiplexer_1_out0,
       demultiplexer_1_out1, demultiplexer_1_out4, demultiplexer_1_out5, demultiplexer_1_out6,
       demultiplexer_1_out8, demultiplexer_1_out9, demultiplexer_1_out10, demultiplexer_1_out12,
       demultiplexer_1_out13, demultiplexer_2_out0, demultiplexer_2_out1, demultiplexer_2_out4,
       demultiplexer_2_out5, demultiplexer_2_out6, demultiplexer_2_out8, demultiplexer_2_out9,
       demultiplexer_2_out10, demultiplexer_2_out12, demultiplexer_2_out13, or_1_out, shifter_1_out,
       shifter_2_out, shifter_3_out, subtractor_1_out, xor_1_out;

  Demultiplexer #(.select(4), .width(32), .tristate("false"), .disabled("Z"), .enable("false")) demultiplexer_1 (
    .out0(demultiplexer_1_out0), .out1(demultiplexer_1_out1), .out4(demultiplexer_1_out4),
    .out5(demultiplexer_1_out5), .out6(demultiplexer_1_out6), .out8(demultiplexer_1_out8),
    .out9(demultiplexer_1_out9), .out10(demultiplexer_1_out10), .out12(demultiplexer_1_out12),
    .out13(demultiplexer_1_out13), .in(A), .sel(ALUctr));  // open: out2, out3, out7, out11, out14, out15
  Demultiplexer #(.select(4), .width(32), .tristate("false"), .disabled("Z"), .enable("false")) demultiplexer_2 (
    .out0(demultiplexer_2_out0), .out1(demultiplexer_2_out1), .out4(demultiplexer_2_out4),
    .out5(demultiplexer_2_out5), .out6(demultiplexer_2_out6), .out8(demultiplexer_2_out8),
    .out9(demultiplexer_2_out9), .out10(demultiplexer_2_out10), .out12(demultiplexer_2_out12),
    .out13(demultiplexer_2_out13), .in(B), .sel(ALUctr));  // open: out2, out3, out7, out11, out14, out15
  Adder #(.width(32)) adder_1 (
    .a(demultiplexer_1_out0), .b(demultiplexer_2_out0), .out(adder_1_out));  // open: cin, cout
  Subtractor #(.width(32)) subtractor_1 (
    .a(demultiplexer_1_out1), .b(demultiplexer_2_out1), .out(subtractor_1_out));  // open: bin, bout
  assign and_1_out = demultiplexer_1_out4 & demultiplexer_2_out4;  // AND_Gate and_1, 32 bits wide
  assign or_1_out = demultiplexer_1_out5 | demultiplexer_2_out5;  // OR_Gate or_1, 32 bits wide
  assign xor_1_out = demultiplexer_1_out6 ^ demultiplexer_2_out6;  // XOR_Gate xor_1, 32 bits wide
  Shifter #(.width(32), .shift("ll")) shifter_1 (
    .in(demultiplexer_1_out8), .\dist (demultiplexer_2_out8[4:0]), .out(shifter_1_out));
  Shifter #(.width(32), .shift("lr")) shifter_2 (
    .in(demultiplexer_1_out9), .\dist (demultiplexer_2_out9[4:0]), .out(shifter_2_out));
  Shifter #(.width(32), .shift("ar")) shifter_3 (
    .in(demultiplexer_1_out10), .\dist (demultiplexer_2_out10[4:0]), .out(shifter_3_out));
  Comparator #(.width(32), .mode("twosComplement")) comparator_1 (
    .a(demultiplexer_1_out12), .b(demultiplexer_2_out12), .lt(comparator_1_lt));  // open: gt, eq
  Comparator #(.width(32), .mode("unsigned")) comparator_2 (
    .a(demultiplexer_1_out13), .b(demultiplexer_2_out13), .lt(comparator_2_lt));  // open: gt, eq
  assign bit_extender_1_out = {{31{1'b0}}, comparator_1_lt};  // Bit_Extender bit_extender_1
  assign bit_extender_2_out = {{31{1'b0}}, comparator_2_lt};  // Bit_Extender bit_extender_2
  Multiplexer #(.select(4), .width(32), .disabled("Z"), .enable("false")) multiplexer_1 (
    .in0(adder_1_out), .in1(subtractor_1_out), .in4(and_1_out), .in5(or_1_out), .in6(xor_1_out),
    .in8(shifter_1_out), .in9(shifter_2_out), .in10(shifter_3_out), .in12(bit_extender_1_out),
    .in13(bit_extender_2_out), .out(Result), .sel(ALUctr));  // open: in2, in3, in7, in11, in14, in15

  // Notes on the sheet:
  //   A: pull=down
  //   B: pull=down
  //   Result: pull=down
  //   输入引脚区
  //   请勿改动引脚区
  //   输出引脚区
  //   ALUctr：ALU操作码列表
  //   0000: add
  //   0001: sub
  //   0100: and
  //   0101: or
  //   0110: xor
  //   1000: sll
  //   1001: srl
  //   1010: sra
  //   1100: slt
  //   1101: sltu
endmodule

module BrCmp (
  input  Unsigned,
  input  [31:0] A,
  input  [31:0] B,
  output BrEq,
  output BrLT
);

  wire comparator_1_eq, comparator_1_lt, comparator_2_eq, comparator_2_lt;
  wire [31:0] demultiplexer_1_out0, demultiplexer_1_out1, demultiplexer_2_out0, demultiplexer_2_out1;

  Demultiplexer #(.select(1), .width(32), .tristate("false"), .disabled("Z"), .enable("false")) demultiplexer_1 (
    .out0(demultiplexer_1_out0), .out1(demultiplexer_1_out1), .in(A), .sel(Unsigned));
  Demultiplexer #(.select(1), .width(32), .tristate("false"), .disabled("Z"), .enable("false")) demultiplexer_2 (
    .out0(demultiplexer_2_out0), .out1(demultiplexer_2_out1), .in(B), .sel(Unsigned));
  Comparator #(.width(32), .mode("twosComplement")) comparator_1 (
    .a(demultiplexer_1_out0), .b(demultiplexer_2_out0), .eq(comparator_1_eq), .lt(comparator_1_lt));  // open: gt
  Comparator #(.width(32), .mode("unsigned")) comparator_2 (
    .a(demultiplexer_1_out1), .b(demultiplexer_2_out1), .eq(comparator_2_eq), .lt(comparator_2_lt));  // open: gt
  Multiplexer #(.select(1), .width(1), .disabled("Z"), .enable("false")) multiplexer_1 (
    .in0(comparator_1_eq), .in1(comparator_2_eq), .out(BrEq), .sel(Unsigned));
  Multiplexer #(.select(1), .width(1), .disabled("Z"), .enable("false")) multiplexer_2 (
    .in0(comparator_1_lt), .in1(comparator_2_lt), .out(BrLT), .sel(Unsigned));

  // Notes on the sheet:
  //   A: pull=down
  //   B: pull=down
  //   输入引脚区
  //   请勿改动引脚区
  //   输出引脚区
endmodule

module ImmGen (
  input  [2:0] Type,
  input  [24:0] Inst25,
  output [31:0] Imm32
);

  wire [3:0] bit_extender_2_out;
  wire [5:0] bit_extender_1_out;
  wire [7:0] bit_extender_3_out;

  assign bit_extender_1_out = {{5{Inst25[24]}}, Inst25[24]};  // Bit_Extender bit_extender_1
  assign bit_extender_2_out = {{3{Inst25[24]}}, Inst25[24]};  // Bit_Extender bit_extender_2
  Multiplexer #(.select(3), .width(6), .disabled("Z"), .enable("false")) multiplexer_1 (
    .in0(bit_extender_1_out), .in1(bit_extender_1_out), .in2(bit_extender_1_out), .in3(bit_extender_1_out),
    .in4(Inst25[23:18]), .in5({6{1'b0}}), .in6({6{1'b0}}), .in7({6{1'b0}}), .out(Imm32[30:25]), .sel(Type));
  assign bit_extender_3_out = {{7{Inst25[24]}}, Inst25[24]};  // Bit_Extender bit_extender_3
  Multiplexer #(.select(3), .width(4), .disabled("Z"), .enable("false")) multiplexer_2 (
    .in0(bit_extender_2_out), .in1(bit_extender_2_out), .in2(bit_extender_2_out), .in3(bit_extender_2_out),
    .in4(Inst25[17:14]), .in5(4'b0000), .in6(4'b0000), .in7(4'b0000), .out(Imm32[24:21]), .sel(Type));
  Multiplexer #(.select(3), .width(1), .disabled("Z"), .enable("false")) multiplexer_3 (
    .in0(Inst25[13]), .in1(Inst25[0]), .in2(1'b0), .in3(1'b0), .in4(1'b0), .in5(1'b0), .in6(1'b0),
    .in7(1'b0), .out(Imm32[0]), .sel(Type));
  Multiplexer #(.select(3), .width(4), .disabled("Z"), .enable("false")) multiplexer_4 (
    .in0(Inst25[17:14]), .in1(Inst25[4:1]), .in2(Inst25[4:1]), .in3(Inst25[17:14]), .in4(4'b0000),
    .in5(4'b0000), .in6(4'b0000), .in7(4'b0000), .out(Imm32[4:1]), .sel(Type));
  Multiplexer #(.select(3), .width(6), .disabled("Z"), .enable("false")) multiplexer_5 (
    .in0(Inst25[23:18]), .in1(Inst25[23:18]), .in2(Inst25[23:18]), .in3(Inst25[23:18]), .in4({6{1'b0}}),
    .in5({6{1'b0}}), .in6({6{1'b0}}), .in7({6{1'b0}}), .out(Imm32[10:5]), .sel(Type));
  Multiplexer #(.select(3), .width(1), .disabled("Z"), .enable("false")) multiplexer_6 (
    .in0(Inst25[13]), .in1(Inst25[13]), .in2(Inst25[0]), .in3(Inst25[24]), .in4(1'b0), .in5(1'b0),
    .in6(1'b0), .in7(1'b0), .out(Imm32[11]), .sel(Type));
  Multiplexer #(.select(3), .width(8), .disabled("Z"), .enable("false")) multiplexer_7 (
    .in0(bit_extender_3_out), .in1(bit_extender_3_out), .in2(bit_extender_3_out), .in3(Inst25[12:5]),
    .in4(Inst25[12:5]), .in5({8{1'b0}}), .in6({8{1'b0}}), .in7({8{1'b0}}), .out(Imm32[19:12]), .sel(Type));
  Multiplexer #(.select(3), .width(1), .disabled("Z"), .enable("false")) multiplexer_8 (
    .in0(Inst25[24]), .in1(Inst25[24]), .in2(Inst25[24]), .in3(Inst25[24]), .in4(Inst25[13]), .in5(1'b0),
    .in6(1'b0), .in7(1'b0), .out(Imm32[20]), .sel(Type));

  assign Imm32[31] = Inst25[24];

  // Notes on the sheet:
  //   Inst25: pull=down
  //   输入引脚区
  //   请勿改动引脚区
  //   输出引脚区
  //   Type：指令格式列表
  //   00: I-Type
  //   01: S-Type
  //   10: B-Type
  //   11: J-Type
endmodule
