// Logisim project FinalProject.circ as structural Verilog
module RV32I (
  input  clk,
  input  [31:0] Addr,
  output [15:0] ICount,
  output [31:0] PCout,
  output [31:0] MData,
  output Halt,
  output [31:0] out
);

  wire brcmp_1_breq, brcmp_1_brlt, controller_1_brun, controller_1_memrw, controller_1_op1sel,
       controller_1_op2sel, controller_1_pcsel, controller_1_regw, not_1_out;
  wire [1:0] controller_1_wbsel;
  wire [2:0] controller_1_immsel;
  wire [3:0] controller_1_aluctr;
  wire [13:0] multiplexer_4_out;
  wire [31:0] adder_1_out, alu_1_result, DMEM_data, immgen_1_imm32, multiplexer_1_out, multiplexer_2_out,
       multiplexer_3_out, rf32_1_rdata1, rf32_1_rdata2, rom_1_data;

  Multiplexer #(.select(1), .width(32), .disabled("Z"), .enable("false")) multiplexer_1 (
    .in0(adder_1_out), .in1(alu_1_result), .out(multiplexer_1_out), .sel(controller_1_pcsel));
  Register #(.width(32), .trigger("rising"), .Select("low")) PC (
    .D(multiplexer_1_out), .en(not_1_out), .Q(PCout), .clk(clk));  // open: clr
  not not_1 (not_1_out, Halt);
  Counter #(.width(16), .max('hffff), .ongoal("wrap"), .trigger("rising"), .behavior("new")) counter_1 (
    .count(not_1_out), .Q(ICount), .clk(clk));  // open: load, D, carry, clr, preset, down
  Adder #(.width(32)) adder_1 (.a(32'h4), .b(PCout), .out(adder_1_out));  // open: cin, cout
  ROM #(.addrWidth(14), .dataWidth(32), .Select("low")) rom_1 (.addr(PCout[15:2]), .data(rom_1_data));
  RF32 rf32_1 (
    .wdata(out), .rdata1(rf32_1_rdata1), .rdata2(rf32_1_rdata2), .rs1(rom_1_data[19:15]),
    .rs2(rom_1_data[24:20]), .rd(rom_1_data[11:7]), .RegW(controller_1_regw), .clk(clk));
  ImmGen immgen_1 (.Inst25(rom_1_data[31:7]), .Imm32(immgen_1_imm32), .Type(controller_1_immsel));
  Controller controller_1 (
    .BrEq(brcmp_1_breq), .BrLT(brcmp_1_brlt), .PCSel(controller_1_pcsel), .RegW(controller_1_regw),
    .ImmSel(controller_1_immsel), .Op1Sel(controller_1_op1sel), .Op2Sel(controller_1_op2sel),
    .BrUn(controller_1_brun), .ALUctr(controller_1_aluctr), .MemRW(controller_1_memrw),
    .WBSel(controller_1_wbsel), .Halt(Halt), .Inst(rom_1_data));
  BrCmp brcmp_1 (
    .A(rf32_1_rdata1), .B(rf32_1_rdata2), .Unsigned(controller_1_brun), .BrEq(brcmp_1_breq),
    .BrLT(brcmp_1_brlt));
  Multiplexer #(.select(1), .width(32), .disabled("Z"), .enable("false")) multiplexer_2 (
    .in0(rf32_1_rdata1), .in1(PCout), .out(multiplexer_2_out), .sel(controller_1_op1sel));
  Multiplexer #(.select(1), .width(32), .disabled("Z"), .enable("false")) multiplexer_3 (
    .in0(immgen_1_imm32), .in1(rf32_1_rdata2), .out(multiplexer_3_out), .sel(controller_1_op2sel));
  ALU alu_1 (.A(multiplexer_2_out), .B(multiplexer_3_out), .Result(alu_1_result), .ALUctr(controller_1_aluctr));
  Multiplexer #(.select(1), .width(14), .disabled("Z"), .enable("false")) multiplexer_4 (
    .in0(alu_1_result[13:0]), .in1(Addr[13:0]), .out(multiplexer_4_out), .sel(Halt));
  RAM #(.addrWidth(14), .dataWidth(32), .bus("separate"), .Select("low")) DMEM (
    .addr(multiplexer_4_out), .din(rf32_1_rdata2), .data(DMEM_data), .str(controller_1_memrw), .clk(clk));  // open: sel, ld, clr
  Multiplexer #(.select(1), .width(32), .disabled("Z"), .enable("false")) multiplexer_5 (
    .in0(DMEM_data), .out(MData), .sel(controller_1_memrw));  // open: in1
  Multiplexer #(.select(2), .width(32), .disabled("Z"), .enable("false")) multiplexer_6 (
    .in0(DMEM_data), .in1(alu_1_result), .in2(adder_1_out), .in3(immgen_1_imm32), .out(out),
    .sel(controller_1_wbsel));

  // Notes on the sheet:
  //   输入引脚区
  //   contents of rom_1 (hex, n*v repeats v):
  //   deadc2b7 eef28293 2337 30313 532023 32383 732223 432e03 103de93 10e1f13 1df6f33 430313 1e32023
  //   a00893 73
  //   注意：你需要在Lab5的基础上，实现LUI指令相关的数据通路和控制逻辑。请你根据需要自行增加数据通路和控制逻辑子电路，但本项目将不对这些子电路单独进行测试。请勿改动引脚区！
  //   输出引脚区
endmodule

module TestRV32I (
  input  [31:0] in_1
);

  wire clock_1_out, rv32i_1_halt;
  wire [15:0] rv32i_1_icount;
  wire [31:0] rv32i_1_mdata, rv32i_1_pcout;

  // Probe on in_1
  Clock #(.highDuration(1), .lowDuration(1)) clock_1 (.out(clock_1_out));
  RV32I rv32i_1 (
    .ICount(rv32i_1_icount), .PCout(rv32i_1_pcout), .MData(rv32i_1_mdata), .Addr(in_1), .clk(clock_1_out),
    .Halt(rv32i_1_halt));  // open: out
  // Probe on rv32i_1_icount
  // Probe on rv32i_1_pcout
  // Probe on rv32i_1_mdata
  // Probe on rv32i_1_halt

  // Notes on the sheet:
  //   RV32I处理器执行的程序为: final-code.asm
  //   在开始仿真测试前，请将Addr输入引脚的值设置为0x2004
  //   执行结束的标志为 Halt=1，执行的正确结果为 MData=0xbeefdead。
  //   注意：该程序中包含LUI指令，因此在你的RV32I中要实现LUI相关的数据通路和控制逻辑。
endmodule

module TestPipeline (
  input  [31:0] in_1
);

  wire clock_1_out, pipeline_1_halt;
  wire [31:0] pipeline_1_mdata, pipeline_1_pcout;

  Pipeline pipeline_1 (
    .PCout(pipeline_1_pcout), .MData(pipeline_1_mdata), .Halt(pipeline_1_halt), .Addr(in_1), .clk(clock_1_out));
  Clock #(.highDuration(1), .lowDuration(1)) clock_1 (.out(clock_1_out));
  // Probe on pipeline_1_pcout
  // Probe on pipeline_1_mdata
  // Probe on pipeline_1_halt

  // Notes on the sheet:
  //   流水线处理器执行同样的程序: final-code.asm
  //   在开始仿真测试前，请将Addr输入引脚的值设置为0x2004
  //   执行结束的标志为 Halt=1，执行的正确结果为 MData=0xbeefdead。
endmodule

// Halt
module Pipeline (
  input  clk,
  input  [31:0] Addr,
  output [31:0] PCout,
  output [31:0] MData,
  output Halt
);

  wire and_1_out, BU_out_4, controller_1_op1sel, controller_1_op2sel, controller_1_regw,
       exe_mem_1_regw_prime, forward_unit_1_fm, id_exe_1_halt_prime, id_exe_1_op1sel_prime,
       id_exe_1_op2sel_prime, id_exe_1_pcsel, id_exe_1_regw_prime, mem_wb_1_regw_prime, not_1_out, not_2_out,
       not_3_out, not_4_out, or_1_out, or_2_out;
  wire [1:0] controller_1_memrw, controller_1_wbsel, exe_mem_1_memrw_prime, exe_mem_1_wbsel_prime,
       forward_unit_1_fa, forward_unit_1_fb, id_exe_1_memrw_prime, id_exe_1_wbsel_prime, mem_wb_1_wbsel_prime;
  wire [2:0] controller_1_cftype, controller_1_immsel, id_exe_1_cftype_prime, id_exe_1_immsel_prime;
  wire [3:0] controller_1_aluctr, id_exe_1_aluctr_prime;
  wire [4:0] exe_mem_1_rd_prime, exe_mem_1_rs2_prime, id_exe_1_inst25_prime, id_exe_1_inst25_prime_3,
       mem_wb_1_rd_prime;
  wire [13:0] exe_mem_1_aluout_prime, multiplexer_6_out;
  wire [24:5] id_exe_1_inst25_prime_2;
  wire [31:0] adder_1_out, alu_1_result, exe_mem_1_imm_prime, exe_mem_1_npc_prime, exe_mem_1_rdata2_prime,
       id_exe_1_npc_prime, id_exe_1_pc_prime, id_exe_1_rd1_prime, id_exe_1_rd2_prime, if_id_1_ir_prime,
       if_id_1_npc_prime, if_id_1_pc_prime, immgen_1_imm32, mem_wb_1_aluout_prime, mem_wb_1_dmout_prime,
       mem_wb_1_imm_prime, mem_wb_1_npc_prime, multiplexer_1_out, multiplexer_2_out, multiplexer_3_out,
       multiplexer_4_out, multiplexer_5_out, multiplexer_7_out, multiplexer_8_out, rf32_1_rdata1,
       rf32_1_rdata2, rom_1_data;
  wire [31:14] exe_mem_1_aluout_prime_2;

  Multiplexer #(.select(1), .width(32), .disabled("Z"), .enable("false")) multiplexer_1 (
    .in0(adder_1_out), .in1(alu_1_result), .out(multiplexer_1_out), .sel(or_1_out));
  Register #(.width(32), .trigger("rising"), .Select("low")) PC (
    .D(multiplexer_1_out), .en(1'b1), .Q(PCout), .clk(and_1_out));  // open: clr
  and and_1 (and_1_out, not_1_out, clk);
  not not_1 (not_1_out, Halt);
  Adder #(.width(32)) adder_1 (.a(32'h4), .b(PCout), .out(adder_1_out));  // open: cin, cout
  or or_1 (or_1_out, BU_out_4, id_exe_1_pcsel, 1'b0);
  IF_ID if_id_1 (
    .NPC(adder_1_out), .PC(PCout), .IR(rom_1_data), .NPC_prime(if_id_1_npc_prime),
    .PC_prime(if_id_1_pc_prime), .IR_prime(if_id_1_ir_prime), .in_4(clk));
  ROM #(.addrWidth(14), .dataWidth(32), .Select("low")) rom_1 (.addr(PCout[15:2]), .data(rom_1_data));
  Controller controller_1 (
    .RegW(controller_1_regw), .ImmSel(controller_1_immsel), .Op1Sel(controller_1_op1sel),
    .Op2Sel(controller_1_op2sel), .ALUctr(controller_1_aluctr), .MemRW(controller_1_memrw),
    .WBSel(controller_1_wbsel), .Halt(Halt), .Inst(if_id_1_ir_prime), .CfType(controller_1_cftype));
  ID_EXE id_exe_1 (
    .CfType_prime(id_exe_1_cftype_prime), .Op1Sel_prime(id_exe_1_op1sel_prime),
    .Op2Sel_prime(id_exe_1_op2sel_prime), .ImmSel_prime(id_exe_1_immsel_prime), .PCsel(id_exe_1_pcsel),
    .ALUctr_prime(id_exe_1_aluctr_prime), .MemRW_prime(id_exe_1_memrw_prime),
    .RegW_prime(id_exe_1_regw_prime), .WBSel_prime(id_exe_1_wbsel_prime), .NPC_prime(id_exe_1_npc_prime),
    .PC_prime(id_exe_1_pc_prime), .Rd1_prime(id_exe_1_rd1_prime), .Rd2_prime(id_exe_1_rd2_prime),
    .Inst25_prime({id_exe_1_inst25_prime_2[24:18], id_exe_1_inst25_prime_3, id_exe_1_inst25_prime_2[12:5], id_exe_1_inst25_prime}),
    .CfType(controller_1_cftype), .Op1Sel(controller_1_op1sel), .Op2Sel(controller_1_op2sel),
    .ImmSel(controller_1_immsel), .ALUctr(controller_1_aluctr), .MemRW(controller_1_memrw),
    .RegW(controller_1_regw), .WBSel(controller_1_wbsel), .NPC(if_id_1_npc_prime), .clk(clk),
    .PC(if_id_1_pc_prime), .Rd1(rf32_1_rdata1), .Rd2(rf32_1_rdata2), .Inst25(if_id_1_ir_prime[31:7]),
    .Halt(Halt), .Halt_prime(id_exe_1_halt_prime));
  RF32 rf32_1 (
    .wdata(multiplexer_8_out), .rdata1(rf32_1_rdata1), .rdata2(rf32_1_rdata2), .rs1(if_id_1_ir_prime[19:15]),
    .rs2(if_id_1_ir_prime[24:20]), .rd(mem_wb_1_rd_prime), .RegW(mem_wb_1_regw_prime), .clk(not_2_out));
  not not_2 (not_2_out, clk);
  Branch_Unit BU (.in_1(id_exe_1_rd1_prime), .in_2(id_exe_1_rd2_prime), .in_3(id_exe_1_cftype_prime), .out_4(BU_out_4));
  Multiplexer #(.select(2), .width(32), .disabled("Z"), .enable("false")) multiplexer_2 (
    .in0(id_exe_1_rd1_prime), .in1(multiplexer_8_out),
    .in2({exe_mem_1_aluout_prime_2, exe_mem_1_aluout_prime}), .in3({32{1'b0}}), .out(multiplexer_2_out),
    .sel(forward_unit_1_fa));
  Multiplexer #(.select(2), .width(32), .disabled("Z"), .enable("false")) multiplexer_3 (
    .in0(id_exe_1_rd2_prime), .in1(multiplexer_8_out),
    .in2({exe_mem_1_aluout_prime_2, exe_mem_1_aluout_prime}), .in3({32{1'b0}}), .out(multiplexer_3_out),
    .sel(forward_unit_1_fb));
  ImmGen immgen_1 (
    .Inst25({id_exe_1_inst25_prime_2[24:18], id_exe_1_inst25_prime_3, id_exe_1_inst25_prime_2[12:5], id_exe_1_inst25_prime}),
    .Imm32(immgen_1_imm32), .Type(id_exe_1_immsel_prime));
  Forward_Unit forward_unit_1 (
    .EX_MEM_RegW(exe_mem_1_regw_prime), .EX_MEM_rd(exe_mem_1_rd_prime), .rs1(id_exe_1_inst25_prime_2[12:8]),
    .rs2(id_exe_1_inst25_prime_3), .MEM_WB_RegW(mem_wb_1_regw_prime), .MEM_WB_rd(mem_wb_1_rd_prime),
    .EX_MEM_MemRW(exe_mem_1_memrw_prime), .EX_MEM_rs2(exe_mem_1_rs2_prime), .FA(forward_unit_1_fa),
    .FB(forward_unit_1_fb), .FM(forward_unit_1_fm));
  Multiplexer #(.select(1), .width(32), .disabled("Z"), .enable("false")) multiplexer_4 (
    .in0(multiplexer_2_out), .in1(id_exe_1_pc_prime), .out(multiplexer_4_out), .sel(id_exe_1_op1sel_prime));
  Multiplexer #(.select(1), .width(32), .disabled("Z"), .enable("false")) multiplexer_5 (
    .in0(immgen_1_imm32), .in1(multiplexer_3_out), .out(multiplexer_5_out), .sel(id_exe_1_op2sel_prime));
  EXE_MEM exe_mem_1 (
    .NPC(id_exe_1_npc_prime), .ALUout(alu_1_result), .Rdata2(id_exe_1_rd2_prime),
    .RegW_prime(exe_mem_1_regw_prime), .WBSel_prime(exe_mem_1_wbsel_prime), .NPC_prime(exe_mem_1_npc_prime),
    .ALUout_prime({exe_mem_1_aluout_prime_2, exe_mem_1_aluout_prime}), .Rdata2_prime(exe_mem_1_rdata2_prime),
    .Rd_prime(exe_mem_1_rd_prime), .MemRW(id_exe_1_memrw_prime), .RegW(id_exe_1_regw_prime),
    .WBSel(id_exe_1_wbsel_prime), .MemRW_prime(exe_mem_1_memrw_prime), .Rd(id_exe_1_inst25_prime), .clk(clk),
    .Imm(immgen_1_imm32), .Imm_prime(exe_mem_1_imm_prime), .rs2(id_exe_1_inst25_prime_3),
    .rs2_prime(exe_mem_1_rs2_prime), .Halt(id_exe_1_halt_prime));  // open: Halt_prime
  ALU alu_1 (.A(multiplexer_4_out), .B(multiplexer_5_out), .Result(alu_1_result), .ALUctr(id_exe_1_aluctr_prime));
  not not_3 (not_3_out, Halt);
  Multiplexer #(.select(1), .width(14), .disabled("Z"), .enable("false")) multiplexer_6 (
    .in0(Addr[13:0]), .in1(exe_mem_1_aluout_prime), .out(multiplexer_6_out), .sel(not_3_out));
  Multiplexer #(.select(1), .width(32), .disabled("Z"), .enable("false")) multiplexer_7 (
    .in0(multiplexer_8_out), .in1(exe_mem_1_rdata2_prime), .out(multiplexer_7_out), .sel(not_4_out));
  not not_4 (not_4_out, forward_unit_1_fm);
  MEM_WB mem_wb_1 (
    .NPC(exe_mem_1_npc_prime), .ALUout({exe_mem_1_aluout_prime_2, exe_mem_1_aluout_prime}), .DMout(MData),
    .NPC_prime(mem_wb_1_npc_prime), .ALUout_prime(mem_wb_1_aluout_prime), .DMout_prime(mem_wb_1_dmout_prime),
    .Rd_prime(mem_wb_1_rd_prime), .RegW(exe_mem_1_regw_prime), .WBSel(exe_mem_1_wbsel_prime),
    .RegW_prime(mem_wb_1_regw_prime), .WBSel_prime(mem_wb_1_wbsel_prime), .Rd(exe_mem_1_rd_prime), .clk(clk),
    .Imm(exe_mem_1_imm_prime), .Imm_prime(mem_wb_1_imm_prime));  // open: Halt_prime, Halt
  RAM #(.addrWidth(14), .dataWidth(32), .bus("separate"), .Select("low")) DMEM (
    .addr(multiplexer_6_out), .din(multiplexer_7_out), .data(MData), .str(exe_mem_1_memrw_prime[1]),
    .clk(clk), .ld(or_2_out));  // open: sel, clr
  or or_2 (or_2_out, exe_mem_1_memrw_prime[0], Halt);
  Multiplexer #(.select(2), .width(32), .disabled("Z"), .enable("false")) multiplexer_8 (
    .in0(mem_wb_1_dmout_prime), .in1(mem_wb_1_aluout_prime), .in2(mem_wb_1_npc_prime),
    .in3(mem_wb_1_imm_prime), .out(multiplexer_8_out), .sel(mem_wb_1_wbsel_prime));

  // Notes on the sheet:
  //   输入引脚区
  //   contents of rom_1 (hex, n*v repeats v):
  //   deadc2b7 eef28293 2337 30313 532023 32383 732223 432e03 103de93 10e1f13 1df6f33 430313 1e32023
  //   a00893 73
  //   注意：你需要实现包含LUI指令的流水线数据通路和控制逻辑。请你根据需要自行增加数据通路和控制逻辑子电路，但本项目将不对这些子电路单独进行测试。请勿改动引脚区！
  //   输出引脚区
  //   ID/EX
  //   Forward Unit
  //   EX/MEM
  //   MEM/WB
endmodule

module Forward_Unit (
  input  EX_MEM_RegW,
  input  [4:0] EX_MEM_rd,
  input  [4:0] rs1,
  input  [4:0] rs2,
  input  MEM_WB_RegW,
  input  [4:0] MEM_WB_rd,
  input  [1:0] EX_MEM_MemRW,
  input  [4:0] EX_MEM_rs2,
  output [1:0] FA,
  output [1:0] FB,
  output FM
);

  wire and_1_out, and_2_out, comparator_1_eq, comparator_2_eq, comparator_3_eq, comparator_4_eq,
       comparator_5_eq, comparator_6_eq, comparator_7_eq, comparator_8_eq, not_1_out, not_2_out;

  Comparator #(.width(1), .mode("unsigned")) comparator_1 (
    .a(MEM_WB_RegW), .b(1'b1), .eq(comparator_1_eq));  // open: gt, lt
  Comparator #(.width(5), .mode("unsigned")) comparator_2 (
    .a(MEM_WB_rd), .b(rs1), .eq(comparator_2_eq));  // open: gt, lt
  Comparator #(.width(5), .mode("unsigned")) comparator_3 (
    .a(MEM_WB_rd), .b(rs2), .eq(comparator_3_eq));  // open: gt, lt
  Comparator #(.width(1), .mode("unsigned")) comparator_4 (
    .a(1'b1), .b(EX_MEM_RegW), .eq(comparator_4_eq));  // open: gt, lt
  Comparator #(.width(5), .mode("unsigned")) comparator_5 (
    .a(EX_MEM_rd), .b(rs1), .eq(comparator_5_eq));  // open: gt, lt
  Comparator #(.width(5), .mode("unsigned")) comparator_6 (
    .a(EX_MEM_rd), .b(rs2), .eq(comparator_6_eq));  // open: gt, lt
  Comparator #(.width(2), .mode("unsigned")) comparator_7 (
    .a(EX_MEM_MemRW), .b(2'b10), .eq(comparator_7_eq));  // open: gt, lt
  Comparator #(.width(5), .mode("unsigned")) comparator_8 (
    .a(EX_MEM_rs2), .b(MEM_WB_rd), .eq(comparator_8_eq));  // open: gt, lt
  and and_1 (and_1_out, comparator_1_eq, comparator_2_eq);
  and and_2 (and_2_out, comparator_1_eq, comparator_3_eq);
  and and_3 (FA[1], comparator_4_eq, comparator_5_eq);
  and and_4 (FB[1], comparator_4_eq, comparator_6_eq);
  not not_1 (not_1_out, FA[1]);
  not not_2 (not_2_out, FB[1]);
  and and_5 (FM, comparator_7_eq, comparator_8_eq);
  and and_6 (FA[0], and_1_out, not_1_out);
  and and_7 (FB[0], and_2_out, not_2_out);
endmodule

module Branch_Unit (
  input  [31:0] in_1,
  input  [31:0] in_2,
  input  [2:0] in_3,
  output out_4
);

  wire comparator_1_eq, comparator_1_lt, comparator_2_lt, not_1_out, not_2_out, not_3_out;

  Comparator #(.width(32), .mode("twosComplement")) comparator_1 (
    .a(in_1), .b(in_2), .eq(comparator_1_eq), .lt(comparator_1_lt));  // open: gt
  Comparator #(.width(32), .mode("unsigned")) comparator_2 (.a(in_1), .b(in_2), .lt(comparator_2_lt));  // open: gt, eq
  not not_1 (not_1_out, comparator_1_lt);
  not not_2 (not_2_out, comparator_2_lt);
  not not_3 (not_3_out, comparator_1_eq);
  Multiplexer #(.select(3), .width(1), .disabled("Z"), .enable("false")) multiplexer_1 (
    .in0(comparator_1_eq), .in1(not_3_out), .in2(1'b0), .in3(1'b1), .in4(comparator_1_lt), .in5(not_1_out),
    .in6(comparator_2_lt), .in7(not_2_out), .out(out_4), .sel(in_3));

  // Other names for the same wires on the sheet: CfType[2:0] = in_3; ID_EX_Rdata1[31:0] = in_1;
  //   ID_EX_Rdata2[31:0] = in_2; PCSel = out_4
endmodule

module IF_ID (
  input  [31:0] NPC,
  input  [31:0] PC,
  input  [31:0] IR,
  input  in_4,
  output [31:0] NPC_prime,
  output [31:0] PC_prime,
  output [31:0] IR_prime
);

  Register #(.width(32), .trigger("rising"), .Select("low")) u_NPC (
    .D(NPC), .Q(NPC_prime), .clk(in_4));  // open: en, clr
  Register #(.width(32), .trigger("rising"), .Select("low")) register_1 (
    .D(PC), .Q(PC_prime), .clk(in_4));  // open: en, clr
  Register #(.width(32), .trigger("rising"), .Select("low")) u_IR (.D(IR), .Q(IR_prime), .clk(in_4));  // open: en, clr

  // Other names for the same wires on the sheet: clk = in_4
endmodule

module ID_EXE (
  input  Halt,
  input  [2:0] CfType,
  input  Op1Sel,
  input  Op2Sel,
  input  [2:0] ImmSel,
  input  [3:0] ALUctr,
  input  [1:0] MemRW,
  input  RegW,
  input  [1:0] WBSel,
  input  clk,
  input  [31:0] NPC,
  input  [31:0] PC,
  input  [31:0] Rd1,
  input  [31:0] Rd2,
  input  [24:0] Inst25,
  output Halt_prime,
  output [2:0] CfType_prime,
  output Op1Sel_prime,
  output Op2Sel_prime,
  output [2:0] ImmSel_prime,
  output PCsel,
  output [3:0] ALUctr_prime,
  output [1:0] MemRW_prime,
  output RegW_prime,
  output [1:0] WBSel_prime,
  output [31:0] NPC_prime,
  output [31:0] PC_prime,
  output [31:0] Rd1_prime,
  output [31:0] Rd2_prime,
  output [24:0] Inst25_prime
);

  Register #(.width(1), .trigger("rising"), .Select("low")) u_Halt (
    .D(Halt), .Q(Halt_prime), .clk(clk));  // open: en, clr
  Register #(.width(3), .trigger("rising"), .Select("low")) u_CfType (
    .D(CfType), .Q(CfType_prime), .clk(clk));  // open: en, clr
  Register #(.width(1), .trigger("rising"), .Select("low")) u_Op1Sel (
    .D(Op1Sel), .Q(Op1Sel_prime), .clk(clk));  // open: en, clr
  Register #(.width(1), .trigger("rising"), .Select("low")) u_Op2Sel (
    .D(Op2Sel), .Q(Op2Sel_prime), .clk(clk));  // open: en, clr
  Register #(.width(3), .trigger("rising"), .Select("low")) u_ImmSel (
    .D(ImmSel), .Q(ImmSel_prime), .clk(clk));  // open: en, clr
  Register #(.width(4), .trigger("rising"), .Select("low")) u_ALUctr (
    .D(ALUctr), .Q(ALUctr_prime), .clk(clk));  // open: en, clr
  Register #(.width(2), .trigger("rising"), .Select("low")) u_MemRW (
    .D(MemRW), .Q(MemRW_prime), .clk(clk));  // open: en, clr
  Register #(.width(1), .trigger("rising"), .Select("low")) u_RegW (
    .D(RegW), .Q(RegW_prime), .clk(clk));  // open: en, clr
  Register #(.width(2), .trigger("rising"), .Select("low")) u_WBSel (
    .D(WBSel), .Q(WBSel_prime), .clk(clk));  // open: en, clr
  Register #(.width(32), .trigger("rising"), .Select("low")) u_NPC (
    .D(NPC), .Q(NPC_prime), .clk(clk));  // open: en, clr
  Register #(.width(32), .trigger("rising"), .Select("low")) u_PC (.D(PC), .Q(PC_prime), .clk(clk));  // open: en, clr
  Register #(.width(32), .trigger("rising"), .Select("low")) u_Rd1 (
    .D(Rd1), .Q(Rd1_prime), .clk(clk));  // open: en, clr
  Register #(.width(32), .trigger("rising"), .Select("low")) u_Rd2 (
    .D(Rd2), .Q(Rd2_prime), .clk(clk));  // open: en, clr
  Register #(.width(25), .trigger("rising"), .Select("low")) instr (
    .D(Inst25), .Q(Inst25_prime), .clk(clk));  // open: en, clr
  Register #(.width(1), .trigger("rising"), .Select("low")) u_PCSel (.D(1'b0), .Q(PCsel), .clk(clk));  // open: en, clr
endmodule

module EXE_MEM (
  input  Halt,
  input  [1:0] MemRW,
  input  RegW,
  input  [1:0] WBSel,
  input  [31:0] NPC,
  input  [31:0] ALUout,
  input  [31:0] Rdata2,
  input  clk,
  input  [4:0] Rd,
  input  [31:0] Imm,
  input  [4:0] rs2,
  output Halt_prime,
  output [1:0] MemRW_prime,
  output RegW_prime,
  output [1:0] WBSel_prime,
  output [31:0] NPC_prime,
  output [31:0] ALUout_prime,
  output [31:0] Rdata2_prime,
  output [4:0] Rd_prime,
  output [31:0] Imm_prime,
  output [4:0] rs2_prime
);

  Register #(.width(32), .trigger("rising"), .Select("low")) u_Imm (
    .D(Imm), .Q(Imm_prime), .clk(clk));  // open: en, clr
  Register #(.width(5), .trigger("rising"), .Select("low")) u_rs2 (.D(rs2), .Q(rs2_prime), .clk(clk));  // open: en, clr
  Register #(.width(1), .trigger("rising"), .Select("low")) u_Halt (
    .D(Halt), .Q(Halt_prime), .clk(clk));  // open: en, clr
  Register #(.width(2), .trigger("rising"), .Select("low")) u_MemRW (
    .D(MemRW), .Q(MemRW_prime), .clk(clk));  // open: en, clr
  Register #(.width(1), .trigger("rising"), .Select("low")) u_RegW (
    .D(RegW), .Q(RegW_prime), .clk(clk));  // open: en, clr
  Register #(.width(2), .trigger("rising"), .Select("low")) u_WBSel (
    .D(WBSel), .Q(WBSel_prime), .clk(clk));  // open: en, clr
  Register #(.width(32), .trigger("rising"), .Select("low")) u_NPC (
    .D(NPC), .Q(NPC_prime), .clk(clk));  // open: en, clr
  Register #(.width(32), .trigger("rising"), .Select("low")) u_ALUout (
    .D(ALUout), .Q(ALUout_prime), .clk(clk));  // open: en, clr
  Register #(.width(32), .trigger("rising"), .Select("low")) u_Rdata2 (
    .D(Rdata2), .Q(Rdata2_prime), .clk(clk));  // open: en, clr
  Register #(.width(5), .trigger("rising"), .Select("low")) u_Rd (.D(Rd), .Q(Rd_prime), .clk(clk));  // open: en, clr
endmodule

// Halt'
module MEM_WB (
  input  Halt,
  input  RegW,
  input  [1:0] WBSel,
  input  [31:0] NPC,
  input  [31:0] ALUout,
  input  [31:0] DMout,
  input  clk,
  input  [4:0] Rd,
  input  [31:0] Imm,
  output Halt_prime,
  output RegW_prime,
  output [1:0] WBSel_prime,
  output [31:0] NPC_prime,
  output [31:0] ALUout_prime,
  output [31:0] DMout_prime,
  output [4:0] Rd_prime,
  output [31:0] Imm_prime
);

  Register #(.width(1), .trigger("rising"), .Select("low")) u_Halt (
    .D(Halt), .Q(Halt_prime), .clk(clk));  // open: en, clr
  Register #(.width(1), .trigger("rising"), .Select("low")) u_RegW (
    .D(RegW), .Q(RegW_prime), .clk(clk));  // open: en, clr
  Register #(.width(2), .trigger("rising"), .Select("low")) u_WBSel (
    .D(WBSel), .Q(WBSel_prime), .clk(clk));  // open: en, clr
  Register #(.width(32), .trigger("rising"), .Select("low")) u_NPC (
    .D(NPC), .Q(NPC_prime), .clk(clk));  // open: en, clr
  Register #(.width(32), .trigger("rising"), .Select("low")) u_ALUout (
    .D(ALUout), .Q(ALUout_prime), .clk(clk));  // open: en, clr
  Register #(.width(32), .trigger("rising"), .Select("low")) u_DMout (
    .D(DMout), .Q(DMout_prime), .clk(clk));  // open: en, clr
  Register #(.width(5), .trigger("rising"), .Select("low")) u_Rd (.D(Rd), .Q(Rd_prime), .clk(clk));  // open: en, clr
  Register #(.width(32), .trigger("rising"), .Select("low")) u_Imm (
    .D(Imm), .Q(Imm_prime), .clk(clk));  // open: en, clr
endmodule
