// Logisim project RV32I-pipeline.circ as structural Verilog: 3 circuits, main circuit Controller
module Controller (
  input  [31:0] Inst,
  output [2:0] CfType,
  output RegW,
  output [2:0] ImmSel,
  output Op1Sel,
  output Op2Sel,
  output [3:0] ALUctr,
  output [1:0] MemRW,
  output [1:0] WBSel,
  output Halt
);

  wire CfType0, CfType1, CfType1_i, CfType1_r, ImmSel1_b, Op1Sel_b, or_8_out, R_type_p1, RD, RegW_i, RegW_r,
       WBSel0_i, WBSel0_r;
  wire [2:0] CfType_b;
  wire [3:0] ALUctr_i, ALUctr_r;

  // PlaRom #(.\and (9), .outputs(7), .Contents("0 1 1 2 1*8 2 1*4 2 0 1 1 2 1*3 2 1 0 1 1 2 1*3 2 2 0 1 1 2 1 1 2 1*5 2 1 1 2 1 2 2 1 1 2 1 1 2 1 2 0 1 1 2 1 1 2 2 1 0 1 1 2 1 1 2*3 1 0*4 1*4 0*3 1*5 0 0 1*5 0 1*4 0 1 1 0 1*4 0 0 1*5 0 1 0 1*3 0 1 0 1*4 0 1 0 0 1 1"), .Select("low")) I_ALU: pin names not known; wires that end beside it: {Inst[30], Inst[6:2], Inst[14:12]}, {WBSel0_i, ALUctr_i, RegW_i, CfType1_i}
  // PlaRom #(.\and (10), .outputs(8), .Contents("1 1 2 2 1*5 2 1 2 2 1*7 2 2 1*4 2 1 1 2 2 1*3 2 1*3 2 2 1*3 2 2 1 1 2 2 1 1 2 1*4 2 2 1 1 2 1 2 2 1 2 2 1 1 2 1 2 1 1 2 2 1 1 2 2 1*3 2 2 1 1 2*3 1 1 0*4 1*4 0*3 1*6 0*3 1*6 0 0 1*6 0 1*5 0 1 1 0 1*5 0 0 1*6 0 1 0 1*4 0 1 0 1*5 0 1 0 0 1 1"), .Select("low")) R_type: pin names not known; wires that end beside it: R_type_p1, {Inst[30], Inst[6:2], Inst[14:12]}, {WBSel0_r, Op2Sel, ALUctr_r, RegW_r, CfType1_r}
  and and_1 (Halt, Inst[6], Inst[5], Inst[4], ~Inst[3], ~Inst[2]);  // AND_Gate
  and JAL (CfType0, Inst[2], Inst[3], ~Inst[4], Inst[5], Inst[6]);  // AND_Gate
  or or_1 (CfType[0], CfType0, CfType_b[0]);
  or or_2 (CfType[1], CfType1, CfType_b[1]);
  or or_3 (CfType[2], CfType_b[2], 1'b0);
  and JALR (CfType0, Inst[2], ~Inst[3], ~Inst[4], Inst[5], Inst[6]);  // AND_Gate
  and LW (MemRW[0], ~Inst[2], ~Inst[3], ~Inst[4], ~Inst[5], ~Inst[6]);  // AND_Gate
  and SW (MemRW[1], ~Inst[2], ~Inst[3], ~Inst[4], Inst[5], ~Inst[6]);  // AND_Gate
  // PlaRom #(.\and (6), .outputs(5), .Contents("2 2 1*6 2 2 1*5 2*3 1*3 2 1 1 2 2 1*3 2 1 2*3 1*3 2 2 1 2 2 1*3 2*3 0*3 1 1 0 0 1*4 0 0 1*3 0 1*5 0 1*7"), .Select("low")) B_type: pin names not known; wires that end beside it: Inst[5], {Inst[6:2], Inst[14:12]}, {CfType_b, Op1Sel_b, ImmSel1_b}
  or or_4 (RD, Inst[7], Inst[8], Inst[9], Inst[10], Inst[11]);
  or or_5 (Op1Sel, CfType0, Op1Sel_b);
  or or_6 (ImmSel[0], CfType0, MemRW[1]);
  or or_7 (ImmSel[1], CfType0, ImmSel1_b);
  or or_8 (or_8_out, MemRW[0], RegW_i, RegW_r, CfType0, CfType0, ImmSel[2]);
  and and_2 (RegW, or_8_out, RD);
  or or_9 (WBSel[0], WBSel0_i, WBSel0_r, ImmSel[2]);
  or or_10 (WBSel[1], CfType0, CfType0, ImmSel[2]);
  assign ALUctr = ALUctr_i | ALUctr_r;  // OR_Gate or_11, 4 bits wide
  and LUI (ImmSel[2], Inst[2], ~Inst[3], Inst[4], Inst[5], ~Inst[6]);  // AND_Gate
  or or_12 (CfType1, CfType1_i, CfType1_r, CfType0, CfType0, MemRW[0], MemRW[1], ImmSel[2]);

  // Other names for the same wires on the sheet: func1 = Inst[30]; Op2Sel_r = Op2Sel; func3[2:0] = Inst[14:12];
  //   opc5[4:0] = Inst[6:2]; ECALL = Halt; CfType1_u = ImmSel[2]; ImmSel2_U = ImmSel[2]; RegW_lui = ImmSel[2];
  //   WBSel0_U = ImmSel[2]; WBSel1_U = ImmSel[2]; rd_t[4:0] = Inst[11:7]; CfType1_lw = MemRW[0]; MemRW0_lw = MemRW[0];
  //   RegW_lw = MemRW[0]; CfType1_s = MemRW[1]; ImmSel0_s = MemRW[1]; MemRW1_s = MemRW[1]; CfType1_j = CfType0;
  //   CfType1_jr = CfType0; ImmSel0_j = CfType0; ImmSel1_j = CfType0; Op1Sel_j = CfType0; RegW_j = CfType0;
  //   RegW_jr = CfType0; WBSel1_j = CfType0; WBSel1_jr = CfType0

  // Notes on the sheet:
  //   Inst: pull=down
  //   输入引脚区
  //   请勿改动引脚区
  //   输出引脚区
endmodule

module RV32I (
  input  clk,
  input  [31:0] Addr,
  output [15:0] ICount,
  output [31:0] PCout,
  output [31:0] MData,
  output Halt
);

  wire brcmp_1_breq, brcmp_1_brlt, not_1_out, undriven, undriven_2, undriven_4, undriven_5, undriven_6,
       undriven_8;
  wire [1:0] undriven_9;
  wire [2:0] undriven_3;
  wire [3:0] undriven_7;
  wire [13:0] multiplexer_4_out;
  wire [31:0] adder_1_out, alu_1_result, DMEM_data, immgen_1_imm32, multiplexer_1_out, multiplexer_2_out,
       multiplexer_3_out, multiplexer_6_out, rf32_1_rdata1, rf32_1_rdata2, rom_1_data;

  Multiplexer #(.select(1), .width(32), .disabled("Z"), .enable("false")) multiplexer_1 (
    .in0(adder_1_out), .in1(alu_1_result), .out(multiplexer_1_out), .sel(undriven));
  not not_1 (not_1_out, Halt);
  Register #(.width(32), .trigger("rising"), .Select("low")) PC (
    .D(multiplexer_1_out), .en(not_1_out), .Q(PCout), .clk(clk));  // open: clr
  Counter #(.width(16), .max('hffff), .ongoal("wrap"), .trigger("rising"), .behavior("new")) counter_1 (
    .count(not_1_out), .Q(ICount), .clk(clk));  // open: load, D, carry, clr, preset, down
  Adder #(.width(32)) adder_1 (.a(32'h4), .b(PCout), .out(adder_1_out));  // open: cin, cout
  ROM #(.addrWidth(14), .dataWidth(32), .Select("low")) rom_1 (.addr(PCout[15:2]), .data(rom_1_data));
  RF32 rf32_1 (
    .wdata(multiplexer_6_out), .rdata1(rf32_1_rdata1), .rdata2(rf32_1_rdata2), .rs1(rom_1_data[19:15]),
    .rs2(rom_1_data[24:20]), .rd(rom_1_data[11:7]), .RegW(undriven_2), .clk(clk));
  ImmGen immgen_1 (.Inst25(rom_1_data[31:7]), .Imm32(immgen_1_imm32), .Type(undriven_3));
  Multiplexer #(.select(1), .width(32), .disabled("Z"), .enable("false")) multiplexer_2 (
    .in0(rf32_1_rdata1), .in1(PCout), .out(multiplexer_2_out), .sel(undriven_4));
  Multiplexer #(.select(1), .width(32), .disabled("Z"), .enable("false")) multiplexer_3 (
    .in0(immgen_1_imm32), .in1(rf32_1_rdata2), .out(multiplexer_3_out), .sel(undriven_5));
  BrCmp brcmp_1 (.A(rf32_1_rdata1), .B(rf32_1_rdata2), .Unsigned(undriven_6), .BrEq(brcmp_1_breq), .BrLT(brcmp_1_brlt));
  ALU alu_1 (.A(multiplexer_2_out), .B(multiplexer_3_out), .Result(alu_1_result), .ALUctr(undriven_7));
  Multiplexer #(.select(1), .width(14), .disabled("Z"), .enable("false")) multiplexer_4 (
    .in0(alu_1_result[15:2]), .in1(Addr[15:2]), .out(multiplexer_4_out), .sel(Halt));
  RAM #(.addrWidth(14), .dataWidth(32), .bus("separate"), .Select("low")) DMEM (
    .addr(multiplexer_4_out), .din(rf32_1_rdata2), .data(DMEM_data), .str(undriven_8), .clk(clk));  // open: sel, ld, clr
  Multiplexer #(.select(1), .width(32), .disabled("Z"), .enable("false")) multiplexer_5 (
    .in0(DMEM_data), .out(MData), .sel(undriven_8));  // open: in1
  Multiplexer #(.select(2), .width(32), .disabled("Z"), .enable("false")) multiplexer_6 (
    .in0(DMEM_data), .in1(alu_1_result), .in2(adder_1_out), .out(multiplexer_6_out), .sel(undriven_9));  // open: in3

  // Notes on the sheet:
  //   输入引脚区
  //   contents of rom_1 (hex, n*v repeats v):
  //   600613 14000ef 40000613 361613 a62023 73 ff010113 112623 812423 912223 1212023 c00433 200293 2544263
  //   fff40613 fddff0ef a004b3 ffe40613 fd1ff0ef a00933 1248533 80006f 100513 c12083 812403 412483 12903
  //   1010113 8067
  //   请勿改动引脚区
  //   输出引脚区
endmodule

module TestRV32I (
  input  [31:0] in_1
);

  wire clock_1_out, rv32i_1_halt;
  wire [15:0] rv32i_1_icount;
  wire [31:0] rv32i_1_mdata, rv32i_1_pcout;

  Clock #(.highDuration(1), .lowDuration(1)) clock_1 (.out(clock_1_out));
  // Probe on rv32i_1_icount
  // Probe on rv32i_1_pcout
  RV32I rv32i_1 (
    .ICount(rv32i_1_icount), .PCout(rv32i_1_pcout), .MData(rv32i_1_mdata), .Addr(in_1), .clk(clock_1_out),
    .Halt(rv32i_1_halt));
  // Probe on rv32i_1_mdata
  // Probe on rv32i_1_halt

  // Notes on the sheet:
  //   RV32I处理器执行的程序为: Fib(6)。
  //   在开始仿真测试前，请将Addr输入引脚的值设置为0x2000
  //   执行结束的标志为 Halt=1，执行的正确结果为 MData=0xd（即十进制的13）。
endmodule
