// Logisim project RV32I.circ as structural Verilog: 4 circuits, main circuit Controller
module Controller (
  input  BrEq,
  input  BrLT,
  input  [31:0] Inst,
  output PCSel,
  output RegW,
  output [2:0] ImmSel,
  output Op1Sel,
  output Op2Sel,
  output BrUn,
  output [3:0] ALUctr,
  output MemRW,
  output [1:0] WBSel,
  output Halt
);

  wire ImmSel0_j, ImmSel1_b, Op1Sel_b, or_6_out, PCSel_b, PCSel_jr, R_type_p1, RD, RegW_i, RegW_lw, RegW_r,
       WBSel0_i, WBSel0_r;
  wire [3:0] ALUctr_i, ALUctr_r;

  // PlaRom #(.\and (9), .outputs(6), .Contents("0 1 1 2 1*8 2 1*4 2 0 1 1 2 1*3 2 1 0 1 1 2 1*3 2 2 0 1 1 2 1 1 2 1*5 2 1 1 2 1 2 2 1 1 2 1 1 2 1 2 0 1 1 2 1 1 2 2 1 0 1 1 2 1 1 2*3 1 0*4 1*3 0*3 1*4 0 0 1*4 0 1*3 0 1 1 0 1*3 0 0 1*4 0 1 0 1 1 0 1 0 1*3 0 1 0 0 1"), .Select("low")) I_ALU: pin names not known; wires that end beside it: {Inst[30], Inst[6:2], Inst[14:12]}, {WBSel0_i, ALUctr_i, RegW_i}
  // PlaRom #(.\and (10), .outputs(7), .Contents("1 1 2 2 1*5 2 1 2 2 1*7 2 2 1*4 2 1 1 2 2 1*3 2 1*3 2 2 1*3 2 2 1 1 2 2 1 1 2 1*4 2 2 1 1 2 1 2 2 1 2 2 1 1 2 1 2 1 1 2 2 1 1 2 2 1*3 2 2 1 1 2*3 1 1 0*4 1*3 0*3 1*5 0*3 1*5 0 0 1*5 0 1*4 0 1 1 0 1*4 0 0 1*5 0 1 0 1*3 0 1 0 1*4 0 1 0 0 1"), .Select("low")) R_type: pin names not known; wires that end beside it: R_type_p1, {Inst[30], Inst[6:2], Inst[14:12]}, {WBSel0_r, Op2Sel, ALUctr_r, RegW_r}
  and and_1 (Halt, Inst[6], Inst[5], Inst[4], ~Inst[3], ~Inst[2]);  // AND_Gate
  and JAL (ImmSel0_j, Inst[2], Inst[3], ~Inst[4], Inst[5], Inst[6]);  // AND_Gate
  and JALR (PCSel_jr, Inst[2], ~Inst[3], ~Inst[4], Inst[5], Inst[6]);  // AND_Gate
  and LW (RegW_lw, ~Inst[2], ~Inst[3], ~Inst[4], ~Inst[5], ~Inst[6]);  // AND_Gate
  and and_2 (MemRW, ~Inst[2], ~Inst[3], ~Inst[4], Inst[5], ~Inst[6]);  // AND_Gate
  // PlaRom #(.\and (24), .outputs(4), .Contents("1 1 2 2 1*8 2 2 1*5 2 1 1 2 2 1*3 2 1*4 2 2 1*3 2 1 2 1 1 2*3 1 1 2 2 1*3 2 2 1*3 2*3 1 2*3 1*7 2*3 1*5 2 1 2*3 1*3 2 1*3 2*3 1*3 2 1 2 1 2*3 1*3 2 2 1 1 2*3 1*3 2*4 1 2 2 1*6 2 1 2 2 1*5 2 2 1 2 2 1*3 2 1 1 2 1 2 2 1*3 2 1 2 2 1 2 2 1*3 2 2 1 2 1 2 2 1*3 2*7 1*6 2*4 1*5 2*5 1*3 2 1 1 2*4 1*3 2 1 2*5 1*3 2 2 1 2*4 1*3 2*3 0 1 1 0 0 1*3 0 1 1 0 0 1*6 0 1*4 0 1 1 0 0 1*3 0 1*3 0 1 1 0 1*7 0 0 1*3 0 1 1 0 0 1 1 0 0 1*6 0 1*4 0 1*3 0 1 1 0 0 1*3 0 1 1 0 1*7 0"), .Select("low")) B_type: pin names not known; wires that end beside it: Inst[5], {BrEq, BrLT, Inst[6:2], Inst[14:12]}, {BrUn, Op1Sel_b, ImmSel1_b, PCSel_b}
  or or_1 (RD, Inst[7], Inst[8], Inst[9], Inst[10], Inst[11]);
  or or_2 (Op1Sel, ImmSel0_j, Op1Sel_b);
  or or_3 (ImmSel[0], ImmSel0_j, MemRW);
  or or_4 (ImmSel[1], ImmSel0_j, ImmSel1_b);
  or or_5 (PCSel, ImmSel0_j, PCSel_jr, PCSel_b);
  or or_6 (or_6_out, RegW_lw, RegW_i, RegW_r, ImmSel0_j, PCSel_jr, ImmSel[2]);
  and and_3 (RegW, or_6_out, RD);
  or or_7 (WBSel[0], WBSel0_i, WBSel0_r, ImmSel[2]);
  or or_8 (WBSel[1], ImmSel0_j, PCSel_jr, ImmSel[2]);
  assign ALUctr = ALUctr_i | ALUctr_r;  // OR_Gate or_9, 4 bits wide
  and LUI (ImmSel[2], Inst[2], ~Inst[3], Inst[4], Inst[5], ~Inst[6]);  // AND_Gate

  // Other names for the same wires on the sheet: func1 = Inst[30]; Op2Sel_r = Op2Sel; func3[2:0] = Inst[14:12];
  //   opc5[4:0] = Inst[6:2]; ECALL = Halt; ImmSel2_U = ImmSel[2]; RegW_lui = ImmSel[2]; WBSel0_U = ImmSel[2];
  //   WBSel1_U = ImmSel[2]; rd_t[4:0] = Inst[11:7]; ImmSel0_s = MemRW; MemRW_s = MemRW; ImmSel1_j = ImmSel0_j;
  //   Op1Sel_j = ImmSel0_j; PCSel_j = ImmSel0_j; RegW_j = ImmSel0_j; WBSel1_j = ImmSel0_j; RegW_jr = PCSel_jr;
  //   WBSel1_jr = PCSel_jr

  // Notes on the sheet:
  //   Inst: pull=down
  //   输入引脚区
  //   请勿改动引脚区
  //   输出引脚区
endmodule

module TestController (
  output [31:0] Inst,
  output BrEq,
  output BrLT,
  output _passed,
  output halt,
  output [14:0] Result
);

  wire clock_1_out, nHalt;
  wire [2:2] ImmSel;
  wire [5:0] tunnel;
  wire [14:0] Result_S;

  Counter #(.width(6), .max('h3f), .ongoal("wrap"), .trigger("rising"), .behavior("old")) counter_1 (
    .count(nHalt), .Q(tunnel), .clk(clock_1_out));  // open: load, D, carry, clr, preset
  Clock #(.highDuration(1), .lowDuration(1)) clock_1 (.out(clock_1_out));
  // Probe on Result
  ROM #(.addrWidth(6), .dataWidth(32), .Select("high")) u_Inst (.addr(tunnel), .data(Inst));
  Comparator #(.width(15), .mode("unsigned")) comparator_1 (.a(Result), .b(Result_S), .eq(_passed));  // open: gt, lt
  ROM #(.addrWidth(6), .dataWidth(1), .Select("high")) u_BrEq (.addr(tunnel), .data(BrEq));
  Controller controller_1 (
    .BrEq(BrEq), .BrLT(BrLT), .PCSel(Result[14]), .RegW(Result[12]), .ImmSel({ImmSel[2], Result[11:10]}),
    .Op1Sel(Result[9]), .Op2Sel(Result[8]), .BrUn(Result[7]), .ALUctr(Result[6:3]), .MemRW(Result[2]),
    .WBSel(Result[1:0]), .Halt(Result[13]), .Inst(Inst));
  ROM #(.addrWidth(6), .dataWidth(1), .Select("high")) u_BrLT (.addr(tunnel), .data(BrLT));
  not not_1 (nHalt, halt);
  Comparator #(.width(6), .mode("twosComplement")) comparator_2 (.a(tunnel), .b(6'b101111), .eq(halt));  // open: gt, lt
  ROM #(.addrWidth(6), .dataWidth(15), .Select("high")) u_Result_S (.addr(tunnel), .data(Result_S));
  // Pins of 2 and 3 bits meet at {ImmSel[2], Result[11:10]}

  // Other names for the same wires on the sheet: Equal = _passed; WBSel[1:0] = Result[1:0]; MemRW = Result[2];
  //   ALUctr[3:0] = Result[6:3]; BrUn = Result[7]; Op2Sel = Result[8]; Op1Sel = Result[9];
  //   ImmSel[1:0] = Result[11:10]; RegW = Result[12]; Halt_t = Result[13]; PCSel = Result[14]

  // Notes on the sheet:
  //   contents of Inst (hex, n*v repeats v):
  //   68000ef 20300e7 6730063 4731e63 4734c63 4735a63 4736863 4737663 4730463 4731263 4734063 2735e63
  //   2736c63 2737a63 2730863 2731663 2734463 2735263 2736063 737e63 730c63 731a63 734863 735663 736463
  //   737263 83a303 63a423 f9c38313 f9c3a313 f9c3b313 f9c3c313 f9c3e313 f9c3f313 a39313 a3d313 40a3d313
  //   1c38333 41c38333 1c39333 1c3a333 1c3b333 1c3c333 1c3d333 41c3d333 1c3e333 1c3f333 73
  //   contents of BrEq (hex, n*v repeats v):
  //   14*0 12*1
  //   contents of BrLT (hex, n*v repeats v):
  //   8*0 6*1 6*0 6*1
  //   Result_S的内容请借助于所给的电子表格自行生成，并通过Load Image加载进来
  //   contents of Result_S (hex, n*v repeats v):
  //   5e02 5002 a00 4a00 a00 4a00 a80 4a80 a00 4a00 4a00 a00 4a80 a80 4a00 a00 a00 4a00 a80 4a80 4a00 a00
  //   4a00 a00 4a80 a80 1000 404 1001 1061 1069 1031 1029 1021 1041 1049 1051 1101 1109 1141 1161 1169
  //   1131 1149 1151 1129 1121 2000
endmodule

module RV32I (
  input  clk,
  input  [31:0] Addr,
  output [15:0] ICount,
  output [31:0] PCout,
  output [31:0] MData,
  output Halt
);

  wire brcmp_1_breq, brcmp_1_brlt, controller_1_brun, controller_1_memrw, controller_1_op1sel,
       controller_1_op2sel, controller_1_pcsel, controller_1_regw, not_1_out;
  wire [1:0] controller_1_wbsel;
  wire [2:0] controller_1_immsel;
  wire [3:0] controller_1_aluctr;
  wire [13:0] multiplexer_4_out;
  wire [31:0] adder_1_out, alu_1_result, DMEM_data, immgen_1_imm32, multiplexer_1_out, multiplexer_2_out,
       multiplexer_3_out, multiplexer_6_out, rf32_1_rdata1, rf32_1_rdata2, rom_1_data;

  Multiplexer #(.select(1), .width(32), .disabled("Z"), .enable("false")) multiplexer_1 (
    .in0(adder_1_out), .in1(alu_1_result), .out(multiplexer_1_out), .sel(controller_1_pcsel));
  not not_1 (not_1_out, Halt);
  Register #(.width(32), .trigger("rising"), .Select("low")) PC (
    .D(multiplexer_1_out), .en(not_1_out), .Q(PCout), .clk(clk));  // open: clr
  Counter #(.width(16), .max('hffff), .ongoal("wrap"), .trigger("rising"), .behavior("new")) counter_1 (
    .count(not_1_out), .Q(ICount), .clk(clk));  // open: load, D, carry, clr, preset, down
  Adder #(.width(32)) adder_1 (.a(32'h4), .b(PCout), .out(adder_1_out));  // open: cin, cout
  ROM #(.addrWidth(14), .dataWidth(32), .Select("low")) rom_1 (.addr(PCout[15:2]), .data(rom_1_data));
  RF32 rf32_1 (
    .wdata(multiplexer_6_out), .rdata1(rf32_1_rdata1), .rdata2(rf32_1_rdata2), .rs1(rom_1_data[19:15]),
    .rs2(rom_1_data[24:20]), .rd(rom_1_data[11:7]), .RegW(controller_1_regw), .clk(clk));
  ImmGen immgen_1 (.Inst25(rom_1_data[31:7]), .Imm32(immgen_1_imm32), .Type(controller_1_immsel));
  Controller controller_1 (
    .BrEq(brcmp_1_breq), .BrLT(brcmp_1_brlt), .PCSel(controller_1_pcsel), .RegW(controller_1_regw),
    .ImmSel(controller_1_immsel), .Op1Sel(controller_1_op1sel), .Op2Sel(controller_1_op2sel),
    .BrUn(controller_1_brun), .ALUctr(controller_1_aluctr), .MemRW(controller_1_memrw),
    .WBSel(controller_1_wbsel), .Halt(Halt), .Inst(rom_1_data));
  Multiplexer #(.select(1), .width(32), .disabled("Z"), .enable("false")) multiplexer_2 (
    .in0(rf32_1_rdata1), .in1(PCout), .out(multiplexer_2_out), .sel(controller_1_op1sel));
  Multiplexer #(.select(1), .width(32), .disabled("Z"), .enable("false")) multiplexer_3 (
    .in0(immgen_1_imm32), .in1(rf32_1_rdata2), .out(multiplexer_3_out), .sel(controller_1_op2sel));
  BrCmp brcmp_1 (
    .A(rf32_1_rdata1), .B(rf32_1_rdata2), .Unsigned(controller_1_brun), .BrEq(brcmp_1_breq),
    .BrLT(brcmp_1_brlt));
  ALU alu_1 (.A(multiplexer_2_out), .B(multiplexer_3_out), .Result(alu_1_result), .ALUctr(controller_1_aluctr));
  Multiplexer #(.select(1), .width(14), .disabled("Z"), .enable("false")) multiplexer_4 (
    .in0(alu_1_result[15:2]), .in1(Addr[15:2]), .out(multiplexer_4_out), .sel(Halt));
  RAM #(.addrWidth(14), .dataWidth(32), .bus("separate"), .Select("low")) DMEM (
    .addr(multiplexer_4_out), .din(rf32_1_rdata2), .data(DMEM_data), .str(controller_1_memrw), .clk(clk));  // open: sel, ld, clr
  Multiplexer #(.select(1), .width(32), .disabled("Z"), .enable("false")) multiplexer_5 (
    .in0(DMEM_data), .out(MData), .sel(controller_1_memrw));  // open: in1
  Multiplexer #(.select(2), .width(32), .disabled("Z"), .enable("false")) multiplexer_6 (
    .in0(DMEM_data), .in1(alu_1_result), .in2(adder_1_out), .out(multiplexer_6_out), .sel(controller_1_wbsel));  // open: in3

  // Notes on the sheet:
  //   输入引脚区
  //   contents of rom_1 (hex, n*v repeats v):
  //   600613 14000ef 40000613 361613 a62023 73 ff010113 112623 812423 912223 1212023 c00433 200293 2544263
  //   fff40613 fddff0ef a004b3 ffe40613 fd1ff0ef a00933 1248533 80006f 100513 c12083 812403 412483 12903
  //   1010113 8067
  //   请勿改动引脚区
  //   输出引脚区
endmodule

module TestRV32I (
  input  [31:0] in_1
);

  wire clock_1_out, rv32i_1_halt;
  wire [15:0] rv32i_1_icount;
  wire [31:0] rv32i_1_mdata, rv32i_1_pcout;

  Clock #(.highDuration(1), .lowDuration(1)) clock_1 (.out(clock_1_out));
  // Probe on rv32i_1_icount
  // Probe on rv32i_1_pcout
  RV32I rv32i_1 (
    .ICount(rv32i_1_icount), .PCout(rv32i_1_pcout), .MData(rv32i_1_mdata), .Addr(in_1), .clk(clock_1_out),
    .Halt(rv32i_1_halt));
  // Probe on rv32i_1_mdata
  // Probe on rv32i_1_halt

  // Notes on the sheet:
  //   RV32I处理器执行的程序为: Fib(6)。
  //   在开始仿真测试前，请将Addr输入引脚的值设置为0x2000
  //   执行结束的标志为 Halt=1，执行的正确结果为 MData=0xd（即十进制的13）。
endmodule
